# Fritzing sketch connection_scheme_gen2 (saved by Fritzing 0.9.5d)
perfboards: 1

parts:
  8_4V_->_5V = LM2596 step down module
  Компонент2 = TE466 [part_number=TE466]
  Steering_control = Basic Servo
  Wheels = DC Motor
  Battery_1 = battery_holder_single_18650
  Battery_2 = battery_holder_single_18650
  2s_BMS = 2S-BMS
  U1 = OV7670 Camera [package=camera_sfv24r-2st_2]
  R1 = Resistor [tolerance=±5% resistance=5100 package=THT]
  R2 = Resistor [tolerance=±5% resistance=5100 package=THT]
  Side_sensor = hc_sro4
  Forward_sensor = hc_sro4
  M1 = DOIT Esp32 DevKit v1 (30 pins long, 11 pins width) [part_number=ESP32S-PIN30]
  Type-C_Female_port = USB_MICROB_PLUG [package=micro-b-smt]
  part = Adafruit INA219 [part_number=INA219]  # not connected

nets:
  N1: 8_4V_->_5V.IN+, Компонент2.Pin_11, Battery_1.+#0, 2s_BMS.pin1
  GND: 8_4V_->_5V.IN-, 8_4V_->_5V.OUT-, Компонент2.Pin_2, Компонент2.Pin_8, Steering_control.gnd, Battery_2.+#1, 2s_BMS.pin2, U1.GND, Side_sensor.GND, Forward_sensor.GND, M1.GND
  VCC: 8_4V_->_5V.OUT+, Компонент2.Pin_1, Steering_control.vcc, Side_sensor.VCC, Forward_sensor.VCC, M1.VIN
  N2: Компонент2.Pin_5, M1.D5
  N3: Компонент2.Pin_6, M1.D26
  N4: Компонент2.Pin_7, M1.D25
  N5: Компонент2.Pin_9, Wheels.pin_2
  N6: Компонент2.Pin_10, Wheels.pin_1
  N7: Steering_control.pulse, M1.D23
  N8: Battery_1.+#1, Battery_2.+#0, 2s_BMS.pin3#4
  N9: 2s_BMS.pin3#2, Type-C_Female_port.GND
  N10: 2s_BMS.pin3#3, Type-C_Female_port.VCC
  3V3: U1.3V3, R1.Pin_0, R2.Pin_0, M1.3V3
  N11: U1.SIOC, R2.Pin_1, M1.D22
  N12: U1.VSYNC, M1.D34
  N13: U1.PCLK, M1.D33
  N14: U1.D7, M1.D4
  N15: U1.D5, M1.D13
  N16: U1.D3, M1.D15
  N17: U1.D1, M1.TX2
  N18: U1.SIDO, R1.Pin_1, M1.D21
  N19: U1.HREF, M1.D35
  N20: U1.XCLK, M1.D32
  N21: U1.D6, M1.D12
  N22: U1.D4, M1.D14
  N23: U1.D2, M1.RX2
  N24: U1.D0, M1.D27

custom parts:
  LM2596 step down module: LM2596 DC-DC step down power supply module 3 A.
  TE466: Description: This is essentially a ramped up version of our Ardumoto motor driver shield. For this monster shield we've replaced the L298 H-bridge with a pair of VNH2SP30 full-bridge motor drivers. We've also beefed up the support circuitry so this board is capable of driving a pair of high-current motors! The VIN and motor out are pitched for our 5mm screw terminals (not included), making it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
  battery_holder_single_18650: single 18650 battery holder
  2S-BMS: 2S-BMS LIPO battery charger / protection unit. Note pcb does not match the board as it will likely connect with wires, so pcb is 5 pads suitable for .1in header pins.
  OV7670 Camera: CMOS image sensor
  DOIT Esp32 DevKit v1 (30 pins long, 11 pins width): The DOIT Esp32 DevKit v1 is one of the development board created by DOIT to evaluate the ESP-WROOM-32 module. It is based on the ESP32 microcontroller that boasts Wifi, Bluetooth, Ethernet and Low Power support all in a single chip. (vanepp) made breadboard work, adjusted pin numbering and labels and reduced size of schematic and cleaned up pcb. This chip is 30pins long (2 x15) and 11 pins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
  Adafruit INA219: This breakout board will solve all your power-monitoring problems. Instead of struggling with two multimeters, you can just use the handy INA219B chip on this breakout to both measure both the high side voltage and DC current draw over I2C with 1% precision. Most current-measuring devices such as our current panel meter are only good for low side measuring. That means that unless you want to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

// code stored in the sketch: washer.ino

